// Logisim project semaforo.circ as structural Verilog: 1 circuit, main circuit main
module main (
  input  S0,
  input  S1,
  output MR,
  output MG,
  output MY,
  output SG,
  output SY,
  output SR,
  output TL,
  output TS
);

  wire not_1_out, not_2_out, not_3_out, not_4_out;

  not not_1 (not_1_out, S0);
  not not_2 (not_2_out, S1);
  not not_3 (not_3_out, S1);
  not not_4 (not_4_out, S0);
  or or_1 (MR, SY, SG);
  and and_1 (MG, not_1_out, not_2_out);
  and and_2 (MY, S0, not_3_out);
  and and_3 (SG, S0, S1);
  and and_4 (SY, S1, not_4_out);
  or or_2 (SR, MY, MG);
  or or_3 (TL, SG, MG);
  or or_4 (TS, SY, MY);
endmodule
