// Logisim project ckt_controle_tanque.circ as structural Verilog: 1 circuit, main circuit main
module main (
  input  Lh,
  input  LI,
  input  Th,
  input  Tc,
  output Ventrada,
  output H,
  output Alarme,
  output \Válvula_de_saída 
);

  wire and_1_out, and_2_out, and_4_out, not_1_out, not_2_out, not_3_out, not_4_out, not_5_out, not_6_out,
       or_1_out, or_2_out;

  not not_1 (not_1_out, Lh);
  not not_2 (not_2_out, Th);
  not not_3 (not_3_out, Tc);
  and and_1 (and_1_out, not_2_out, Tc);
  not not_4 (not_4_out, Th);
  not not_5 (not_5_out, Tc);
  or or_1 (or_1_out, not_2_out, not_3_out);
  or or_2 (or_2_out, LI, not_1_out);
  not not_6 (not_6_out, LI);
  and and_2 (and_2_out, not_4_out, not_5_out);
  and and_3 (Ventrada, not_1_out, or_1_out);
  and and_4 (and_4_out, Lh, not_6_out);
  and and_5 (\Válvula_de_saída , LI, and_2_out);
  and and_6 (H, or_2_out, and_1_out);
  or or_3 (Alarme, Th, and_4_out);

  // Notes on the sheet:
  //   Válvula de entrada
  //   Elemento de aquecimento
endmodule
