// Logisim project bitwise-and.circ as structural Verilog: 1 circuit, main circuit main
module main (
  input  A3,
  input  B3,
  input  A2,
  input  B2,
  input  A1,
  input  B1,
  input  A0,
  input  B0,
  output S3,
  output S2,
  output S1,
  output S0
);

  and and_1 (S3, A3, B3);
  and and_2 (S2, A2, B2);
  and and_3 (S1, A1, B1);
  and and_4 (S0, A0, B0);
endmodule
