// Logisim project full-adder.circ as structural Verilog: 1 circuit, main circuit main
module main (
  input  A3,
  input  B3,
  input  A2,
  input  B2,
  input  A1,
  input  B1,
  input  A0,
  input  B0,
  input  Cin,
  output Cout,
  output S3,
  output S2,
  output S1,
  output S0
);

  wire FA_2_cout, FA_3_cout, FA_4_cout, xor_1_out, xor_2_out, xor_3_out, xor_4_out;

  xor xor_1 (xor_1_out, B3, Cin);
  xor xor_2 (xor_2_out, B2, Cin);
  xor xor_3 (xor_3_out, B1, Cin);
  xor xor_4 (xor_4_out, B0, Cin);
  adder_1_bit_main FA (.A(A3), .B(xor_1_out), .CIN(FA_2_cout), .S(S3), .Cout(Cout));
  adder_1_bit_main FA_2 (.A(A2), .B(xor_2_out), .CIN(FA_3_cout), .S(S2), .Cout(FA_2_cout));
  adder_1_bit_main FA_3 (.A(A1), .B(xor_3_out), .CIN(FA_4_cout), .S(S1), .Cout(FA_3_cout));
  adder_1_bit_main FA_4 (.A(A0), .B(xor_4_out), .CIN(Cin), .S(S0), .Cout(FA_4_cout));
endmodule
