// Logisim project adder-1-bit.circ as structural Verilog: 1 circuit, main circuit main
module main (
  input  A,
  input  B,
  input  CIN,
  output S,
  output Cout
);

  wire and_1_out, and_2_out, or_1_out, xor_1_out;

  xor xor_1 (xor_1_out, A, B);
  or or_1 (or_1_out, A, B);
  and and_1 (and_1_out, A, B);
  and and_2 (and_2_out, or_1_out, CIN);
  xor xor_2 (S, xor_1_out, CIN);
  or or_2 (Cout, and_2_out, and_1_out);
endmodule
