// Logisim project ula-completa.circ as structural Verilog: 1 circuit, main circuit main
module main (
  input  A3,
  input  B3,
  input  A2,
  input  B2,
  input  sel,
  input  A1,
  input  B1,
  input  A0,
  input  B0,
  input  Cin,
  output Cout,
  output S3,
  output S2,
  output S1,
  output S0
);

  wire [3:0] AND_s0, FA_s0;

  bitwise_and_main AND (
    .A3(A3), .B3(B3), .A2(A2), .B2(B2), .A1(A1), .B1(B1), .A0(A0), .B0(B0), .S3(AND_s0[3]), .S2(AND_s0[2]),
    .S1(AND_s0[1]), .S0(AND_s0[0]));
  full_adder_main FA (
    .A3(A3), .B3(B3), .A2(A2), .B2(B2), .A1(A1), .B1(B1), .A0(A0), .B0(B0), .Cin(Cin), .Cout(Cout),
    .S3(FA_s0[3]), .S2(FA_s0[2]), .S1(FA_s0[1]), .S0(FA_s0[0]));
  Multiplexer #(.width(4)) multiplexer_1 (.in0(AND_s0), .in1(FA_s0), .out({S3, S2, S1, S0}), .sel(sel));  // open: en
endmodule
