// Logisim project ckt_ventrada_h.circ as structural Verilog: 1 circuit, main circuit main
module main (
  input  Lh,
  input  LI,
  input  Th,
  input  Tc,
  output Ventrada,
  output H
);

  wire and_1_out, not_1_out, not_2_out, not_3_out, or_1_out, or_2_out;

  not not_1 (not_1_out, Lh);
  not not_2 (not_2_out, Th);
  not not_3 (not_3_out, Tc);
  and and_1 (and_1_out, not_2_out, Tc);
  or or_1 (or_1_out, not_2_out, not_3_out);
  or or_2 (or_2_out, LI, not_1_out);
  and and_2 (Ventrada, not_1_out, or_1_out);
  and and_3 (H, or_2_out, and_1_out);

  // Notes on the sheet:
  //   Válvula de entrada
  //   Elemento de aquecimento
endmodule
