// Logisim project ckt_vsaida_a.circ as structural Verilog: 1 circuit, main circuit main
module main (
  input  Lh,
  input  Ll,
  input  Th,
  input  Tc,
  output Alarme,
  output \Válvula_de_saída 
);

  wire and_1_out, and_2_out, not_1_out, not_2_out, not_3_out;

  not not_1 (not_1_out, Th);
  not not_2 (not_2_out, Tc);
  not not_3 (not_3_out, Ll);
  and and_1 (and_1_out, not_1_out, not_2_out);
  and and_2 (and_2_out, Lh, not_3_out);
  and and_3 (\Válvula_de_saída , Ll, and_1_out);
  or or_1 (Alarme, Th, and_2_out);
endmodule
